# Fritzing sketch Thermostat-Wifi-schematic (saved by Fritzing 0.9.3b)
breadboards: 1

parts:
  WeMos_D1 = WeMos D1 Mini
  R1 = Rotary Potentiometer (Large) [maximum_resistance=10kΩ package=THT]
  Temperature_Sensor = TMP36 [package=to-92-kit]
  LCD_Screen = LCD screen
  R2 = Resistor [tolerance=±5% resistance=220 package=THT]
  HC-SR04 = HC-SR04 Ultrasonic Distance Sensor

nets:
  5V: WeMos_D1.5V, R1.leg2, LCD_Screen.VDD, R2.Pin_0, HC-SR04.VCC
  N1: WeMos_D1.A0, Temperature_Sensor.VOUT
  N2: WeMos_D1.D0, LCD_Screen.RS
  N3: WeMos_D1.D1, LCD_Screen.E
  N4: WeMos_D1.D2, LCD_Screen.DB4
  N5: WeMos_D1.D3, LCD_Screen.DB5
  N6: WeMos_D1.D4, LCD_Screen.DB6
  N7: WeMos_D1.D5, LCD_Screen.DB7
  N8: WeMos_D1.D6, HC-SR04.TRIG
  N9: WeMos_D1.D7, HC-SR04.GND
  GND: R1.leg1, Temperature_Sensor.GND, LCD_Screen.VSS, LCD_Screen.R/W, LCD_Screen.LED-, HC-SR04.ECHO
  N10: R1.wiper, LCD_Screen.V0
  3.3V: Temperature_Sensor.VCC
  N11: LCD_Screen.LED+, R2.Pin_1

notes:
  Thermostat-Wifi, Thermostat-Wifi Implementation Schematic using Wemos D1., 1
