# Fritzing sketch Thermostat (saved by Fritzing 0.9.3b)
breadboards: 1

parts:
  Schematic_1 = Arduino Uno (Rev3)
  Temperature_Sensor = TMP36 [package=to-92-kit]
  LCD_Screen = LCD screen
  R1 = Rotary Potentiometer (Small) [maximum_resistance=10kΩ package=THT]
  R2 = Resistor [tolerance=±5% resistance=220 package=THT]
  HC-SR04 = HC-SR04 Ultrasonic Distance Sensor
  R3 = Resistor [tolerance=±5% resistance=220 package=THT]
  R4 = Resistor [tolerance=±5% resistance=220 package=THT]
  R5 = Resistor [tolerance=±5% resistance=220 package=THT]
  LED1 = LED - 5mm [color="Red (633nm)" package="5 mm [THT]"]
  LED2 = LED - 5mm [color="Blue (505nm)" package="5 mm [THT]"]
  LED3 = LED - 5mm [color="Green (565nm)" package="5 mm [THT]"]

nets:
  N1: Schematic_1.A0, Temperature_Sensor.VOUT
  N2: Schematic_1.D8, R4.Pin_1
  N3: Schematic_1.D9_PWM, R3.Pin_1
  N4: Schematic_1.D11_PWM/MOSI, LCD_Screen.E
  N5: Schematic_1.D12/MISO, LCD_Screen.RS
  N6: Schematic_1.D13/SCK, R5.Pin_1
  GND: Schematic_1.GND, Temperature_Sensor.GND, LCD_Screen.VSS, LCD_Screen.R/W, LCD_Screen.LED-, R1.leg1, HC-SR04.ECHO, LED1.cathode, LED2.cathode, LED3.cathode
  N7: Schematic_1.D2, LCD_Screen.DB7
  N8: Schematic_1.D3_PWM, LCD_Screen.DB6
  N9: Schematic_1.D4, LCD_Screen.DB5
  N10: Schematic_1.D5_PWM, LCD_Screen.DB4
  N11: Schematic_1.D6_PWM, HC-SR04.GND
  N12: Schematic_1.D7, HC-SR04.TRIG
  5V: Schematic_1.5V, Temperature_Sensor.VCC, LCD_Screen.VDD, R1.leg2, R2.Pin_1, HC-SR04.VCC
  N13: LCD_Screen.V0, R1.wiper
  N14: LCD_Screen.LED+, R2.Pin_0
  N15: R3.Pin_0, LED1.anode
  N16: R4.Pin_0, LED2.anode
  N17: R5.Pin_0, LED3.anode

notes:
  
  Τhermostat, 1
